// Logisim project 4_Bit_ALU.circ as structural Verilog: 1 circuit, main circuit main
module main (
  input  [2:0] in_1,
  input  A0,
  input  B0,
  input  F,
  input  in_5,
  input  Cin,
  input  A3,
  input  A1,
  input  A2,
  input  B3,
  input  B1,
  input  B2,
  input  in_13,
  input  in_14,
  input  in_15,
  input  in_16,
  input  in_17,
  input  in_18,
  output out_19
);

  wire and_1_out, and_2_out, and_3_out, and_4_out, and_5_out, and_7_out, and_8_out, and_9_out, and_10_out,
       and_11_out, and_13_out, and_14_out, and_15_out, and_16_out, and_17_out, and_19_out, and_20_out,
       and_21_out, and_22_out, and_23_out, B0_Out, B1_Out, B2_Out, B3_Out, Cin_t, not_1_out, not_2_out,
       not_3_out, not_4_out, not_5_out, not_6_out, not_7_out, not_8_out, not_9_out, not_10_out, not_11_out,
       not_12_out, or_3_out, or_6_out, or_9_out;
  wire [3:0] ADD_SUB_Out, ALS, AND_Out, ARS, OR_Out, undriven, undriven_2, XOR_Out;

  not not_1 (not_1_out, B0);
  Multiplexer multiplexer_1 (.in0(B0), .in1(not_1_out), .out(B0_Out), .sel(F));
  Multiplexer multiplexer_2 (.in0(in_5), .in1(Cin), .out(Cin_t), .sel(F));
  Multiplexer #(.select(2), .width(4)) multiplexer_3 (
    .in0({A3, A2, A1, A0}), .in1({A2, A1, A0, in_13}), .in2({A1, A0, in_15, in_14}),
    .in3({A0, in_18, in_17, in_16}), .out(ALS), .sel({B1, B0}));
  not not_2 (not_2_out, A0);
  not not_3 (not_3_out, B0);
  and and_1 (and_1_out, not_2_out, B0);
  and and_2 (and_2_out, A0, not_3_out);
  xor xor_1 (ADD_SUB_Out[0], A0, B0_Out, Cin_t);
  and and_3 (and_3_out, A0, B0_Out);
  and and_4 (and_4_out, B0_Out, Cin_t);
  and and_5 (and_5_out, A0, Cin_t);
  or or_1 (XOR_Out[0], and_1_out, and_2_out);
  or or_2 (OR_Out[0], A0, B0);
  and and_6 (AND_Out[0], A0, B0);
  or or_3 (or_3_out, and_3_out, and_4_out, and_5_out);
  not not_4 (not_4_out, A1);
  not not_5 (not_5_out, B1);
  and and_7 (and_7_out, A1, B1_Out);
  and and_8 (and_8_out, A1, or_3_out);
  and and_9 (and_9_out, B1_Out, or_3_out);
  Multiplexer multiplexer_4 (.in0(B1), .in1(not_6_out), .out(B1_Out), .sel(F));
  not not_6 (not_6_out, B1);
  and and_10 (and_10_out, not_4_out, B1);
  and and_11 (and_11_out, A1, not_5_out);
  or or_4 (OR_Out[1], A1, B1);
  and and_12 (AND_Out[1], A1, B1);
  xor xor_2 (ADD_SUB_Out[1], A1, B1_Out, or_3_out);
  Multiplexer #(.select(2), .width(4)) multiplexer_5 (
    .in0({A3, A2, A1, A0}), .in1({{2{A3}}, A2, A1}), .in2({{3{A3}}, A2}), .in3({4{A3}}), .out(ARS),
    .sel({B1, B0}));
  or or_5 (XOR_Out[1], and_10_out, and_11_out);
  not not_7 (not_7_out, A2);
  not not_8 (not_8_out, B2);
  or or_6 (or_6_out, and_7_out, and_8_out, and_9_out);
  and and_13 (and_13_out, not_7_out, B2);
  and and_14 (and_14_out, A2, not_8_out);
  xor xor_3 (ADD_SUB_Out[2], A2, B2_Out, or_6_out);
  and and_15 (and_15_out, A2, B2_Out);
  and and_16 (and_16_out, A2, or_6_out);
  and and_17 (and_17_out, B2_Out, or_6_out);
  Multiplexer multiplexer_6 (.in0(B2), .in1(not_9_out), .out(B2_Out), .sel(F));
  not not_9 (not_9_out, B2);
  or or_7 (XOR_Out[2], and_13_out, and_14_out);
  or or_8 (OR_Out[2], A2, B2);
  and and_18 (AND_Out[2], A2, B2);
  or or_9 (or_9_out, and_15_out, and_16_out, and_17_out);
  not not_10 (not_10_out, A3);
  not not_11 (not_11_out, B3);
  and and_19 (and_19_out, not_10_out, B3);
  and and_20 (and_20_out, A3, not_11_out);
  xor xor_4 (ADD_SUB_Out[3], A3, B3_Out, or_9_out);
  and and_21 (and_21_out, A3, B3_Out);
  and and_22 (and_22_out, A3, or_9_out);
  and and_23 (and_23_out, B3_Out, or_9_out);
  Multiplexer multiplexer_7 (.in0(B3), .in1(not_12_out), .out(B3_Out), .sel(F));
  not not_12 (not_12_out, B3);
  or or_10 (OR_Out[3], A3, B3);
  and and_24 (AND_Out[3], A3, B3);
  or or_11 (XOR_Out[3], and_19_out, and_20_out);
  or or_12 (out_19, and_21_out, and_22_out, and_23_out);
  Multiplexer #(.select(3), .width(4)) multiplexer_8 (
    .in0(AND_Out), .in1(OR_Out), .in2(XOR_Out), .in3(ADD_SUB_Out), .in4(ALS), .in5(ARS), .in6(undriven),
    .in7(undriven_2), .sel(in_1));  // open: out
  // NoConnect on undriven
  // NoConnect on undriven_2

  // Other names for the same wires on the sheet: ALS_1[3:0] = {A2, A1, A0, in_13};
  //   ALS_2[3:0] = {A1, A0, in_15, in_14}; ALS_3[3:0] = {A0, in_18, in_17, in_16}; ALS_0[3:0] = {A3, A2, A1, A0};
  //   ARS_0[3:0] = {A3, A2, A1, A0}; ARS_1[3:0] = {{2{A3}}, A2, A1}; ARS_2[3:0] = {{3{A3}}, A2}; ARS_3[3:0] = {4{A3}}

  // Notes on the sheet:
  //   Arithmetic Left Shift
  //   Addition
  //   1 Bit OR
  //   1 Bit AND
  //   1 Bit XOR
  //   Arithmetic Right Shift
  //   1 Bit OR
  //   1 Bit AND
  //   1 Bit XOR
  //   1 Bit OR
  //   1 Bit AND
  //   1 Bit XOR
  //   1 Bit OR
  //   1 Bit AND
  //   1 Bit XOR
  //   Select Bits
endmodule
